# Fritzing sketch sketch (saved by Fritzing 0.9.3b)

parts:
  Componente1 = Arduino Nano (Rev3.0)
  Componente2 = Analog Digital MUX Breakout
  Componente3 = Analog Digital MUX Breakout
  Componente4 = Analog Digital MUX Breakout
  Componente5 = Analog Digital MUX Breakout
  Componente6 = ws2812b [package="smd 2812b"]
  Componente7 = ws2812b [package="smd 2812b"]
  Power_plug1 = Power plug
  Componente8 = ws2812b [package="smd 2812b"]

nets:
  N1: Componente1.D7, Componente6.DIN
  N2: Componente1.D9, Componente2.S0, Componente3.S0, Componente4.S0, Componente5.S0
  N3: Componente1.D10, Componente2.S1, Componente3.S1, Componente4.S1, Componente5.S1
  N4: Componente1.D11/MOSI, Componente2.S2, Componente3.S2, Componente4.S2, Componente5.S2
  N5: Componente1.D12/MISO, Componente2.S3, Componente3.S3, Componente4.S3, Componente5.S3
  GND: Componente1.GND, Componente2.GND, Componente2.EN, Componente3.GND, Componente4.GND, Componente4.EN, Componente5.GND, Componente5.EN, Componente6.VSS, Componente7.VSS, Power_plug1.GND, Componente8.VSS
  VCC: Componente1.5V, Componente2.VCC, Componente3.VCC, Componente5.VCC
  N6: Componente1.A3, Componente4.SIG
  N7: Componente1.A2, Componente3.SIG
  N8: Componente1.A1, Componente2.SIG
  N9: Componente1.A0, Componente5.SIG
  VDD: Componente6.VDD, Componente7.VDD, Power_plug1.VCC, Componente8.VDD
  N10: Componente6.DOUT, Componente7.DIN
  N11: Componente7.DOUT, Componente8.DIN
