# Fritzing sketch sketch_2 (saved by Fritzing 0.9.3b)

parts:
  Componente1 = Arduino Nano (Rev3.0) (ICSP)
  U1 = mystery part, 15 pins [chip_label=?]
  U2 = mystery part, 15 pins [chip_label=?]
  MUX1 = 74HC4051 [package="DIP (Dual Inline) [THT]"]
  SS49E_1 = Mystery Part - 3 pins [chip_label=SS49E package=THT]
  SS49E_2 = Mystery Part - 3 pins [chip_label=SS49E package=THT]
  SS49E_3 = Mystery Part - 3 pins [chip_label=SS49E package=THT]
  SS49E_4 = Mystery Part - 3 pins [chip_label=SS49E package=THT]
  SS49E_5 = Mystery Part - 3 pins [chip_label=SS49E package=THT]
  SS49E_6 = Mystery Part - 3 pins [chip_label=SS49E package=THT]
  SS49E_7 = Mystery Part - 3 pins [chip_label=SS49E package=THT]
  SS49E_8 = Mystery Part - 3 pins [chip_label=SS49E package=THT]
  MUX2 = 74HC4051 [package="DIP (Dual Inline) [THT]"]
  SS49E_9 = Mystery Part - 3 pins [chip_label=SS49E package=THT]
  SS49E_10 = Mystery Part - 3 pins [chip_label=SS49E package=THT]
  SS49E_11 = Mystery Part - 3 pins [chip_label=SS49E package=THT]
  SS49E_12 = Mystery Part - 3 pins [chip_label=SS49E package=THT]
  SS49E_13 = Mystery Part - 3 pins [chip_label=SS49E package=THT]
  SS49E_14 = Mystery Part - 3 pins [chip_label=SS49E package=THT]
  SS49E_15 = Mystery Part - 3 pins [chip_label=SS49E package=THT]
  SS49E_16 = Mystery Part - 3 pins [chip_label=SS49E package=THT]
  MUX3 = 74HC4051 [package="DIP (Dual Inline) [THT]"]
  SS49E_17 = Mystery Part - 3 pins [chip_label=SS49E package=THT]
  SS49E_18 = Mystery Part - 3 pins [chip_label=SS49E package=THT]
  SS49E_19 = Mystery Part - 3 pins [chip_label=SS49E package=THT]
  SS49E_20 = Mystery Part - 3 pins [chip_label=SS49E package=THT]
  SS49E_21 = Mystery Part - 3 pins [chip_label=SS49E package=THT]
  SS49E_22 = Mystery Part - 3 pins [chip_label=SS49E package=THT]
  SS49E_23 = Mystery Part - 3 pins [chip_label=SS49E package=THT]
  SS49E_24 = Mystery Part - 3 pins [chip_label=SS49E package=THT]
  MUX4 = 74HC4051 [package="DIP (Dual Inline) [THT]"]
  SS49E_25 = Mystery Part - 3 pins [chip_label=SS49E package=THT]
  SS49E_26 = Mystery Part - 3 pins [chip_label=SS49E package=THT]
  SS49E_27 = Mystery Part - 3 pins [chip_label=SS49E package=THT]
  SS49E_28 = Mystery Part - 3 pins [chip_label=SS49E package=THT]
  SS49E_29 = Mystery Part - 3 pins [chip_label=SS49E package=THT]
  SS49E_30 = Mystery Part - 3 pins [chip_label=SS49E package=THT]
  SS49E_31 = Mystery Part - 3 pins [chip_label=SS49E package=THT]
  SS49E_32 = Mystery Part - 3 pins [chip_label=SS49E package=THT]
  MUX5 = 74HC4051 [package="DIP (Dual Inline) [THT]"]
  MUX6 = 74HC4051 [package="DIP (Dual Inline) [THT]"]
  MUX7 = 74HC4051 [package="DIP (Dual Inline) [THT]"]
  MUX8 = 74HC4051 [package="DIP (Dual Inline) [THT]"]
  SS49E_33 = Mystery Part - 3 pins [chip_label=SS49E package=THT]
  SS49E_34 = Mystery Part - 3 pins [chip_label=SS49E package=THT]
  SS49E_35 = Mystery Part - 3 pins [chip_label=SS49E package=THT]
  SS49E_36 = Mystery Part - 3 pins [chip_label=SS49E package=THT]
  SS49E_37 = Mystery Part - 3 pins [chip_label=SS49E package=THT]
  SS49E_38 = Mystery Part - 3 pins [chip_label=SS49E package=THT]
  SS49E_39 = Mystery Part - 3 pins [chip_label=SS49E package=THT]
  SS49E_40 = Mystery Part - 3 pins [chip_label=SS49E package=THT]
  SS49E_41 = Mystery Part - 3 pins [chip_label=SS49E package=THT]
  SS49E_42 = Mystery Part - 3 pins [chip_label=SS49E package=THT]
  SS49E_43 = Mystery Part - 3 pins [chip_label=SS49E package=THT]
  SS49E_44 = Mystery Part - 3 pins [chip_label=SS49E package=THT]
  SS49E_45 = Mystery Part - 3 pins [chip_label=SS49E package=THT]
  SS49E_46 = Mystery Part - 3 pins [chip_label=SS49E package=THT]
  SS49E_47 = Mystery Part - 3 pins [chip_label=SS49E package=THT]
  SS49E_48 = Mystery Part - 3 pins [chip_label=SS49E package=THT]
  SS49E_49 = Mystery Part - 3 pins [chip_label=SS49E package=THT]
  SS49E_50 = Mystery Part - 3 pins [chip_label=SS49E package=THT]
  SS49E_51 = Mystery Part - 3 pins [chip_label=SS49E package=THT]
  SS49E_52 = Mystery Part - 3 pins [chip_label=SS49E package=THT]
  SS49E_53 = Mystery Part - 3 pins [chip_label=SS49E package=THT]
  SS49E_54 = Mystery Part - 3 pins [chip_label=SS49E package=THT]
  SS49E_55 = Mystery Part - 3 pins [chip_label=SS49E package=THT]
  SS49E_56 = Mystery Part - 3 pins [chip_label=SS49E package=THT]
  SS49E_57 = Mystery Part - 3 pins [chip_label=SS49E package=THT]
  SS49E_58 = Mystery Part - 3 pins [chip_label=SS49E package=THT]
  SS49E_59 = Mystery Part - 3 pins [chip_label=SS49E package=THT]
  SS49E_60 = Mystery Part - 3 pins [chip_label=SS49E package=THT]
  SS49E_61 = Mystery Part - 3 pins [chip_label=SS49E package=THT]
  SS49E_62 = Mystery Part - 3 pins [chip_label=SS49E package=THT]
  SS49E_63 = Mystery Part - 3 pins [chip_label=SS49E package=THT]
  SS49E_64 = Mystery Part - 3 pins [chip_label=SS49E package=THT]

nets:
  N1: Componente1.D1/TX, U2.pin15
  N2: Componente1.D0/RX, U2.pin14
  N3: Componente1.RESET, U1.pin3, U2.pin13
  N4: Componente1.GND, U1.pin2, U2.pin12
  N5: Componente1.D2, U2.pin11
  N6: Componente1.D3, U2.pin10
  N7: Componente1.D4, U2.pin9
  N8: Componente1.D5, U2.pin8
  N9: Componente1.D6, U2.pin7
  N10: Componente1.D7, U2.pin6
  N11: Componente1.D8, U2.pin5
  N12: Componente1.D9, U2.pin4
  N13: Componente1.D10, U2.pin3
  N14: Componente1.D11/MOSI, U2.pin2
  N15: Componente1.D12/MISO, U2.pin1
  N16: Componente1.VIN, U1.pin1
  VCC: Componente1.5V, U1.pin4, MUX1.VDD, SS49E_1.Vcc, SS49E_2.Vcc, SS49E_3.Vcc, SS49E_4.Vcc, SS49E_5.Vcc, SS49E_6.Vcc, SS49E_7.Vcc, SS49E_8.Vcc
  N17: Componente1.A7, U1.pin5
  N18: Componente1.A6, U1.pin6
  N19: Componente1.A5, U1.pin7
  N20: Componente1.A4, U1.pin8
  N21: Componente1.A3, U1.pin9
  N22: Componente1.A2, U1.pin10
  N23: Componente1.A1, U1.pin11
  N24: Componente1.A0, U1.pin12
  N25: Componente1.AREF, U1.pin13
  N26: Componente1.3V3, U1.pin14
  N27: Componente1.D13/SCK, U1.pin15
  N28: MUX1.IO4, SS49E_5.Output
  N29: MUX1.IO6, SS49E_7.Output
  N30: MUX1.IO7, SS49E_8.Output
  N31: MUX1.IO5, SS49E_6.Output
  N32: MUX1.VEE, MUX1.VSS, SS49E_1.Ground, SS49E_2.Ground, SS49E_3.Ground, SS49E_4.Ground, SS49E_5.Ground, SS49E_6.Ground, SS49E_7.Ground, SS49E_8.Ground
  N33: MUX1.IO3, SS49E_4.Output
  N34: MUX1.IO0, SS49E_1.Output
  N35: MUX1.IO1, SS49E_2.Output
  N36: MUX1.IO2, SS49E_3.Output
  N37: MUX2.IO4, SS49E_16.Output
  N38: MUX2.IO6, SS49E_15.Output
  N39: MUX2.IO7, SS49E_10.Output
  N40: MUX2.IO5, SS49E_14.Output
  N41: MUX2.VEE, MUX2.VSS, SS49E_9.Ground, SS49E_10.Ground, SS49E_11.Ground, SS49E_12.Ground, SS49E_13.Ground, SS49E_14.Ground, SS49E_15.Ground, SS49E_16.Ground
  N42: MUX2.IO3, SS49E_11.Output
  N43: MUX2.IO0, SS49E_12.Output
  N44: MUX2.IO1, SS49E_9.Output
  N45: MUX2.IO2, SS49E_13.Output
  VCC_2: MUX2.VDD, SS49E_9.Vcc, SS49E_10.Vcc, SS49E_11.Vcc, SS49E_12.Vcc, SS49E_13.Vcc, SS49E_14.Vcc, SS49E_15.Vcc, SS49E_16.Vcc
  N46: MUX3.IO4, SS49E_19.Output
  N47: MUX3.IO7, SS49E_18.Output
  N48: MUX3.IO5, SS49E_22.Output
  N49: MUX3.VEE, MUX3.VSS, SS49E_17.Ground, SS49E_18.Ground, SS49E_19.Ground, SS49E_20.Ground, SS49E_21.Ground, SS49E_22.Ground, SS49E_23.Ground, SS49E_24.Ground
  N50: MUX3.IO3, SS49E_21.Output
  N51: MUX3.IO0, SS49E_24.Output
  N52: MUX3.IO1, SS49E_23.Output
  N53: MUX3.IO2, SS49E_20.Output
  VCC_3: MUX3.VDD, SS49E_17.Vcc, SS49E_18.Vcc, SS49E_19.Vcc, SS49E_20.Vcc, SS49E_21.Vcc, SS49E_22.Vcc, SS49E_23.Vcc, SS49E_24.Vcc
  N54: MUX4.IO4, SS49E_31.Output
  N55: MUX4.IO7, SS49E_28.Output
  N56: MUX4.IO5, SS49E_27.Output
  N57: MUX4.VEE, MUX4.VSS, SS49E_25.Ground, SS49E_26.Ground, SS49E_27.Ground, SS49E_28.Ground, SS49E_29.Ground, SS49E_30.Ground, SS49E_31.Ground, SS49E_32.Ground
  N58: MUX4.IO3, SS49E_32.Output
  N59: MUX4.IO0, SS49E_25.Output
  N60: MUX4.IO1, SS49E_26.Output
  N61: MUX4.IO2, SS49E_30.Output
  VCC_4: MUX4.VDD, SS49E_25.Vcc, SS49E_26.Vcc, SS49E_27.Vcc, SS49E_28.Vcc, SS49E_29.Vcc, SS49E_30.Vcc, SS49E_31.Vcc, SS49E_32.Vcc
  N62: MUX5.IO4, SS49E_38.Output
  N63: MUX5.IO7, SS49E_55.Output
  N64: MUX5.IO5, SS49E_50.Output
  N65: MUX5.VEE, MUX5.VSS, SS49E_35.Ground, SS49E_38.Ground, SS49E_41.Ground, SS49E_50.Ground, SS49E_52.Ground, SS49E_55.Ground, SS49E_57.Ground, SS49E_61.Ground
  N66: MUX5.IO3, SS49E_52.Output
  N67: MUX5.IO0, SS49E_41.Output
  N68: MUX5.IO1, SS49E_61.Output
  N69: MUX5.IO2, SS49E_35.Output
  VCC_5: MUX5.VDD, SS49E_35.Vcc, SS49E_38.Vcc, SS49E_41.Vcc, SS49E_50.Vcc, SS49E_52.Vcc, SS49E_55.Vcc, SS49E_57.Vcc, SS49E_61.Vcc
  N70: MUX6.IO4, SS49E_46.Output
  N71: MUX6.IO7, SS49E_51.Output
  N72: MUX6.IO5, SS49E_62.Output
  N73: MUX6.VEE, MUX6.VSS, SS49E_36.Ground, SS49E_46.Ground, SS49E_49.Ground, SS49E_51.Ground, SS49E_53.Ground, SS49E_58.Ground, SS49E_62.Ground, SS49E_64.Ground
  N74: MUX6.IO3, SS49E_58.Output
  N75: MUX6.IO0, SS49E_64.Output
  N76: MUX6.IO1, SS49E_49.Output
  N77: MUX6.IO2, SS49E_53.Output
  VCC_6: MUX6.VDD, SS49E_36.Vcc, SS49E_46.Vcc, SS49E_49.Vcc, SS49E_51.Vcc, SS49E_53.Vcc, SS49E_58.Vcc, SS49E_62.Vcc, SS49E_64.Vcc
  N78: MUX7.IO4, SS49E_63.Output
  N79: MUX7.IO7, SS49E_37.Output
  N80: MUX7.IO5, SS49E_59.Output
  N81: MUX7.VEE, MUX7.VSS, SS49E_34.Ground, SS49E_37.Ground, SS49E_39.Ground, SS49E_40.Ground, SS49E_44.Ground, SS49E_56.Ground, SS49E_59.Ground, SS49E_63.Ground
  N82: MUX7.IO3, SS49E_44.Output
  N83: MUX7.IO0, SS49E_39.Output
  N84: MUX7.IO1, SS49E_56.Output
  N85: MUX7.IO2, SS49E_40.Output
  VCC_7: MUX7.VDD, SS49E_34.Vcc, SS49E_37.Vcc, SS49E_39.Vcc, SS49E_40.Vcc, SS49E_44.Vcc, SS49E_56.Vcc, SS49E_59.Vcc, SS49E_63.Vcc
  N86: MUX8.IO4, SS49E_33.Output
  N87: MUX8.IO6, SS49E_45.Output
  N88: MUX8.IO7, SS49E_60.Output
  N89: MUX8.IO5, SS49E_47.Output
  N90: MUX8.VEE, MUX8.VSS, SS49E_33.Ground, SS49E_42.Ground, SS49E_43.Ground, SS49E_45.Ground, SS49E_47.Ground, SS49E_48.Ground, SS49E_54.Ground, SS49E_60.Ground
  N91: MUX8.IO3, SS49E_48.Output
  N92: MUX8.IO0, SS49E_43.Output
  N93: MUX8.IO1, SS49E_42.Output
  N94: MUX8.IO2, SS49E_54.Output
  VCC_8: MUX8.VDD, SS49E_33.Vcc, SS49E_42.Vcc, SS49E_43.Vcc, SS49E_45.Vcc, SS49E_47.Vcc, SS49E_48.Vcc, SS49E_54.Vcc, SS49E_60.Vcc

custom parts:
  74HC4051: 8 channel analog multiplexer/demultiplexer
  Mystery Part - 3 pins: A dummy, proxy, ersatz, stand-in part for whatever you want. With 3 pins on a 100 mil inline pin header footprint.
